# Fritzing sketch Medical device (saved by Fritzing 0.9.10b)

parts:
  MH-ET_LIVE_ESP32_DEVKIT1 = MH-ET LIVE ESP32 DEVKIT 38 pins
  M1 = MakerFocus MAX30102
  DHT11 = Humidity and Temperature Sensor RHT03
  Mod1 = AD8232 HeartRate Monitor [part_number=SEN-12650]
  Part1 = Arduino Uno (Rev3) - ICSP
  SEN1 = Pulse Sensor [package=SIP]
  Part2 = LCD1602-I2C
  Buzzer = Passive Buzzer

nets:
  3V3: MH-ET_LIVE_ESP32_DEVKIT1.3V3, M1.VIN, DHT11.Vcc
  N1: MH-ET_LIVE_ESP32_DEVKIT1.IO32, DHT11.Data-signal
  N2: MH-ET_LIVE_ESP32_DEVKIT1.GND#58, DHT11.GND_1
  5V: MH-ET_LIVE_ESP32_DEVKIT1.5V, Part1.5V, SEN1.Vcc, Part2.VCC
  N3: MH-ET_LIVE_ESP32_DEVKIT1.GND#64, M1.GND
  N4: MH-ET_LIVE_ESP32_DEVKIT1.IO22, M1.SCL
  N5: MH-ET_LIVE_ESP32_DEVKIT1.IO21, M1.SDA
  GND: MH-ET_LIVE_ESP32_DEVKIT1.GND#70, Mod1.GND, Part1.GND, SEN1.GND, Part2.GND, Buzzer.-
  3.3V: Mod1.3.3v, Part1.3V3
  N6: Mod1.OUTPUT, Part1.A1
  N7: Mod1.LO-, Part1.D9_PWM
  N8: Mod1.LO+, Part1.D8
  N9: Part1.A0, SEN1.Signal
  N10: Part1.A4/SDA, Part2.SDA
  N11: Part1.A5/SCL, Part2.SCL
  N12: Part1.D3_PWM, Buzzer.S

custom parts:
  MH-ET LIVE ESP32 DEVKIT 38 pins: http://mh.nodebb.com/topic/2/mh-et-live-esp32-devkit
  MakerFocus MAX30102: Oximeter module using the MAX30102 chip. As usual, if you want the mounting holes in pcb, you need to drag a hole over the pad in silkscreen to actually drill the hole (by default they are not drilled)
  AD8232 HeartRate Monitor: Sparkfun single lead heart rate monitor - Ad8232.
  Pulse Sensor: Pulse Sensor Optical Heart Rate Monitor for Arduino and other microcontrollers
  LCD1602-I2C: A standard character display, usually with 2x16 characters. Comes in many colors with LCM1602 IIC attached.
